# Fritzing sketch Fritzing (saved by Fritzing 0.9.3b)
breadboards: 1

parts:
  S1 = Pushbutton [package="[THT]"]
  S2 = Pushbutton [package="[THT]"]
  S3 = Pushbutton [package="[THT]"]
  Q1 = Basic FET P-Channel [package="TO220 [THT]"]
  D1 = Rectifier Diode [part_number=1N4001 package="300 mil [THT]"]
  LED1 = LED - 5mm [color="Red (633nm)" package="5 mm [THT]"]
  LED2 = LED - 5mm [color="Yellow (595nm)" package="5 mm [THT]"]
  LED3 = LED - 5mm [color="Green (570nm)" package="5 mm [THT]"]
  Часть1 = Arduino Uno (Rev3)
  R1 = Resistor [tolerance=±5% resistance=220 package=THT]
  M1 = DC Motor

nets:
  N1: S1.Pin_1, S1.Pin_2, Часть1.D2
  N2: S1.Pin_3, S1.Pin_4, S2.Pin_3, S2.Pin_4, S3.Pin_3, S3.Pin_4, D1.anode, Часть1.GND, R1.Pin_1, M1.pin_2
  N3: S2.Pin_1, S2.Pin_2, Часть1.D3_PWM
  N4: S3.Pin_1, S3.Pin_2, Часть1.D4
  N5: Q1.gate, Часть1.D9_PWM
  N6: Q1.drain, Часть1.VIN
  N7: Q1.source, D1.cathode, M1.pin_1
  N8: LED1.cathode, LED2.cathode, LED3.cathode, R1.Pin_0
  N9: LED1.anode, Часть1.D7
  N10: LED2.anode, Часть1.D6_PWM
  N11: LED3.anode, Часть1.D5_PWM
